// Logisim project UART_Controller.circ as structural Verilog: 1 circuit, main circuit uart
module uart (
  input  clock,
  input  I_Osel,
  input  rd_wr,
  input  [15:0] Idata,
  input  [7:0] I_Oaddr,
  output dt,
  output con,
  output [7:0] Odata
);

  wire and_1_out, and_2_out, and_4_out, uart_1_p7;
  wire [7:0] uart_1_p1, uart_1_p2;

  assign Odata = and_1_out ? uart_1_p1 : 8'bz;  // Controlled_Buffer controlled_buffer_1
  and and_1 (and_1_out, rd_wr, uart_1_p7);
  // UART uart_1: pin names not known; wires that end beside it: uart_1_p1, uart_1_p2, dt, clock, rd_wr, con, uart_1_p7
  and and_2 (and_2_out, ~rd_wr, uart_1_p7);  // AND_Gate
  assign uart_1_p2 = and_2_out ? Idata[7:0] : 8'bz;  // Controlled_Buffer controlled_buffer_2
  and and_3 (uart_1_p7, and_4_out, I_Osel);
  and and_4 (and_4_out, ~I_Oaddr[7], I_Oaddr[6], I_Oaddr[5], I_Oaddr[4], I_Oaddr[3], ~I_Oaddr[2], I_Oaddr[1], ~I_Oaddr[0]);  // AND_Gate

  // Notes on the sheet:
  //   To interrupt arbiter
endmodule
