// Logisim project main.circ as structural Verilog: 1 circuit, main circuit main
module main (
  input  in_1,
  input  play,
  input  [8:0] in_3,
  input  [8:0] in_4
);

  wire and_1_out, cdm_16_1_p4, cdm_16_1_p5, cdm_16_1_p7, cdm_16_1_p8, cdm_16_1_p10, cdm_16_1_p11, clock, con,
       dt, HS, I_Osel, IAck, in_out_prime, IRQ, mem, not_1_out, RAM, word;
  wire [1:0] cdm_16_1_p9;
  wire [5:0] vec;
  wire [15:0] adr, cdm_16_1_p16, cdm_16_1_p17, data;
  wire [31:0] main_1_out_11, main_1_out_12, main_1_out_13, main_1_out_14, main_1_out_15, main_1_out_16,
       main_1_out_17, main_1_out_18, main_1_out_19, main_1_out_20, main_1_out_21, main_1_out_22,
       main_1_out_23, main_1_out_24, main_1_out_25, main_1_out_26, main_1_out_27, main_1_out_28,
       main_1_out_29, main_1_out_30, main_1_out_31, main_1_out_32, main_1_out_33, main_1_out_34,
       main_1_out_35, main_1_out_36, main_1_out_37, main_1_out_38, main_1_out_39, main_1_out_40,
       main_1_out_41, main_1_out_42;

  // Probe on cdm_16_1_p4
  // Probe on cdm_16_1_p5
  // CdM_16 cdm_16_1: pin names not known; wires that end beside it: IRQ, vec, IAck, cdm_16_1_p4, cdm_16_1_p5, clock, cdm_16_1_p7, cdm_16_1_p8, cdm_16_1_p9, cdm_16_1_p10, cdm_16_1_p11, mem, in_out_prime, word, adr, cdm_16_1_p16, cdm_16_1_p17
  Clock clock_1 (.out(clock));
  Button Hard_reset (.out(HS));
  // Probe on cdm_16_1_p8
  // Probe on cdm_16_1_p7
  // Probe on cdm_16_1_p9
  // Probe on cdm_16_1_p10
  // Probe on cdm_16_1_p11
  // Probe on adr
  assign data = not_1_out ? cdm_16_1_p16 : 16'bz;  // Controlled_Buffer controlled_buffer_1
  not not_1 (not_1_out, in_out_prime);
  assign cdm_16_1_p17 = in_out_prime ? data : 16'bz;  // Controlled_Buffer controlled_buffer_2
  IntArb intarb_1 (.IRQ(IRQ), .vec(vec), .IAck(IAck), .status(cdm_16_1_p9), .clock(clock), .dt(dt), .con(in_1));
  ExpMatrixcontroller_main main_1 (
    .in_out_prime(in_out_prime), .I_Oaddr(adr[7:0]), .I_Osel(I_Osel), .I_Odat(data), .reset(HS), .play(play),
    .surv(in_3), .born(in_4), .I_Odat_2(data), .out_11(main_1_out_11), .out_12(main_1_out_12),
    .out_13(main_1_out_13), .out_14(main_1_out_14), .out_15(main_1_out_15), .out_16(main_1_out_16),
    .out_17(main_1_out_17), .out_18(main_1_out_18), .out_19(main_1_out_19), .out_20(main_1_out_20),
    .out_21(main_1_out_21), .out_22(main_1_out_22), .out_23(main_1_out_23), .out_24(main_1_out_24),
    .out_25(main_1_out_25), .out_26(main_1_out_26), .out_27(main_1_out_27), .out_28(main_1_out_28),
    .out_29(main_1_out_29), .out_30(main_1_out_30), .out_31(main_1_out_31), .out_32(main_1_out_32),
    .out_33(main_1_out_33), .out_34(main_1_out_34), .out_35(main_1_out_35), .out_36(main_1_out_36),
    .out_37(main_1_out_37), .out_38(main_1_out_38), .out_39(main_1_out_39), .out_40(main_1_out_40),
    .out_41(main_1_out_41), .out_42(main_1_out_42), .clock(clock));
  DotMatrix #(.inputtype("row"), .matrixcols(32), .matrixrows(32)) dotmatrix_1 (
    .row0(main_1_out_11), .row1(main_1_out_12), .row2(main_1_out_13), .row3(main_1_out_14),
    .row4(main_1_out_15), .row5(main_1_out_16), .row6(main_1_out_17), .row7(main_1_out_18),
    .row8(main_1_out_19), .row9(main_1_out_20), .row10(main_1_out_21), .row11(main_1_out_22),
    .row12(main_1_out_23), .row13(main_1_out_24), .row14(main_1_out_25), .row15(main_1_out_26),
    .row16(main_1_out_27), .row17(main_1_out_28), .row18(main_1_out_29), .row19(main_1_out_30),
    .row20(main_1_out_31), .row21(main_1_out_32), .row22(main_1_out_33), .row23(main_1_out_34),
    .row24(main_1_out_35), .row25(main_1_out_36), .row26(main_1_out_37), .row27(main_1_out_38),
    .row28(main_1_out_39), .row29(main_1_out_40), .row30(main_1_out_41), .row31(main_1_out_42));
  // RAM ram_1: pin names not known; wires that end beside it: adr, word, RAM, clock, in_out_prime, data
  // Probe on data
  and and_1 (and_1_out, adr[8], adr[9], adr[10], adr[11], adr[12], adr[13], adr[14], adr[15]);
  and and_2 (RAM, ~and_1_out, mem);  // AND_Gate
  Pull_Resistor pull_resistor_1 (.node(data[8]));
  Pull_Resistor pull_resistor_2 (.node(data[9]));
  Pull_Resistor pull_resistor_3 (.node(data[10]));
  Pull_Resistor pull_resistor_4 (.node(data[11]));
  Pull_Resistor pull_resistor_5 (.node(data[12]));
  Pull_Resistor pull_resistor_6 (.node(data[13]));
  Pull_Resistor pull_resistor_7 (.node(data[14]));
  Pull_Resistor pull_resistor_8 (.node(data[15]));
  and and_3 (I_Osel, mem, and_1_out);
  uart uart_1 (
    .Odata(data[7:0]), .Idata(data), .I_Oaddr(adr[7:0]), .dt(dt), .con(con), .clock(clock),
    .rd_wr(in_out_prime), .I_Osel(I_Osel));

  // Other names for the same wires on the sheet: I_Odat[15:0] = data; I_Oaddr[7:0] = adr[7:0];
  //   rd_wr_prime = in_out_prime

  // Notes on the sheet:
  //   UART
endmodule
